# Fritzing sketch AmpliMic (saved by Fritzing 0.8.3b)
circuit board: 16.9333cm x 5.64444cm
breadboards: 1

parts:
  U1 = LM 358 Dual Op-Amp [package="DIP8 [THT]"]
  R1 = Trimmer Potentiometer [maximum_resistance=10kΩ package=THT]
  C1 = Electrolytic Capacitor [capacitance=1000μF package="1010 [SMD, electrolytic]"]
  MIC1 = Microphone
  C2 = Ceramic Capacitor [capacitance=47µF package="1206 [SMD, multilayer]"]
  R2 = Resistor [tolerance=±5% resistance=10 package=THT]
  VCC1 = 4 x AAA Battery Mount
  C3 = Electrolytic Capacitor [capacitance=10μF package="0605 [SMD, electrolytic]"]
  C7 = Electrolytic Capacitor [capacitance=100µF package="200 mil [THT, electrolytic]"]
  C9 = Ceramic Capacitor [capacitance="100 nF" package="0603 [SMD, multilayer]"]

nets:
  N1: U1.connector0, C2.0
  N2: U1.connector1, R1.leg2, VCC1.+, C7.+, C9.0
  N3: U1.connector3, C3.+
  N4: U1.connector5, U1.connector7, MIC1.pin1, R2.Pin_1, VCC1.-, C3.-, C7.-, C9.1
  N5: U1.connector6, C1.-
  N6: R1.wiper, C1.+, MIC1.pin2
  N7: C2.1, R2.Pin_0
